# Fritzing sketch z-axes-connectors (saved by Fritzing 0.9.3b)
stripboards: 4

parts:
  J2 = female pin header, 4 pins [form="♀ (female)"]
  J4 = female pin header, 4 pins [form="♀ (female)"]
  J5 = female pin header, 2 pins [form="♀ (female)"]
  J7 = female pin header, 4 pins [form="♀ (female)"]
  J8 = female pin header, 4 pins [form="♀ (female)"]
  J9 = female pin header, 2 pins [form="♀ (female)"]
  J11 = female pin header, 3 pins [form="♀ (female)"]
  J12 = female pin header, 3 pins [form="♀ (female)"]
  J13 = female pin header, 5 pins [form="♀ (female)"]
  J14 = female pin header, 2 pins [form="♀ (female)"]
  J15 = female pin header, 2 pins [form="♀ (female)"]
  J16 = female pin header, 5 pins [form="♀ (female)"]
  J6 = female pin header, 1 pin [form="♀ (female)"]
  Part2 = Arduino Mega 2560 (Rev3)  # not connected
  Part3 = Arduino Due (Rev2b)
  Part5 = Arduino Ethernet Shield (Rev3)  # not connected
  Part6 = RAMPS 1.4 Shield for Arduino Mega 2560
  proto1 = Adafruit_PermaProto_1_4_Board
  Part8 = Logic Level Converter  # not connected
  J17 = female pin header, 2 pins [form="♀ (female)"]  # not connected
  OLED1 = OLED 128x64 I2C Monochrome Display
  J18 = female pin header, 7 pins [form="♀ (female)"]  # not connected
  J19 = female pin header, 7 pins [form="♀ (female)"]  # not connected
  J20 = female pin header, 2 pins [form="♀ (female)"]  # not connected
  Part9 = BME280 Breakout
  Part10 = Thumb Joystick
  J23 = female pin header, 7 pins [form="♀ (female)"]  # not connected
  J24 = female pin header, 7 pins [form="♀ (female)"]  # not connected
  J21 = female pin header, 3 pins [form="♀ (female)"]  # not connected
  J22 = female pin header, 3 pins [form="♀ (female)"]  # not connected
  J25 = female pin header, 3 pins [form="♀ (female)"]  # not connected
  J26 = female pin header, 3 pins [form="♀ (female)"]  # not connected
  R1 = Resistor [tolerance=±5% resistance=330 package=THT]
  R3 = Trimmer Potentiometer [maximum_resistance=10kΩ package=THT]
  J28 = female pin header, 2 pins [form="♀ (female)"]
  J27 = female pin header, 6 pins [form="♀ (female)"]
  R4 = Resistor [tolerance=±5% resistance=100 package=THT]
  LCD1 = LCD screen
  U1 = Sharp PC817 [package=THT]
  U2 = Sharp PC817 [package=THT]
  U3 = Sharp PC817 [package=THT]
  R5 = Resistor [tolerance=±5% resistance=1k package=THT]
  R6 = Resistor [tolerance=±5% resistance=1k package=THT]
  R7 = Resistor [tolerance=±5% resistance=1k package=THT]
  R8 = Resistor [tolerance=±5% resistance=220 package=THT]
  R9 = Resistor [tolerance=±5% resistance=220 package=THT]
  R10 = Resistor [tolerance=±5% resistance=220 package=THT]
  J29 = female pin header, 2 pins [form="♀ (female)"]
  J30 = female pin header, 2 pins [form="♀ (female)"]
  J31 = female pin header, 2 pins [form="♀ (female)"]
  D2F1 = D2F-FL Omron Snap Action Limit Switch with Level
  D2F2 = D2F-FL Omron Snap Action Limit Switch with Level
  D2F3 = D2F-FL Omron Snap Action Limit Switch with Level
  J32 = double row female pin header, 10 pins [form="♀ (female)"]
  J33 = double row female pin header, 10 pins [form="♀ (female)"]
  J34 = Basic Servo
  D2F4 = D2F-FL Omron Snap Action Limit Switch with Level
  J35 = double row female pin header, 6 pins [form="♀ (female)"]
  J36 = double row female pin header, 6 pins [form="♀ (female)"]

nets:
  N1: J2.pin1, J13.pin3, J16.pin3, J32.pin8, J34.gnd, D2F4.COM
  N2: J2.pin2, J4.pin2, J34.pulse, J35.pin4
  N3: J2.pin3, J4.pin3, D2F4.NC, J35.pin5
  N4: J2.pin4, J4.pin4, J34.vcc, J35.pin6
  N5: J4.pin1, J5.pin1, J6.pin1, J32.pin3
  N6: J5.pin2, J13.pin4, J16.pin4, J32.pin9
  N7: J7.pin1, J8.pin1
  N8: J7.pin2, J8.pin2
  N9: J7.pin3, J8.pin3
  N10: J7.pin4, J8.pin4
  N11: J9.pin1, J11.pin1, J12.pin1, J32.pin4
  N12: J9.pin2, J11.pin2, J12.pin2, J32.pin5
  N13: J11.pin3, J12.pin3, J13.pin2, J16.pin2, J32.pin7
  N14: J13.pin1, J15.pin1, J16.pin1, J32.pin6
  N15: J13.pin5, J14.pin2, J16.pin5, J32.pin10
  N16: J14.pin1, J15.pin2
  N17: Part3.A8, J36.pin4
  N18: Part3.A0, Part10.HORZ
  N19: Part3.A1, Part10.VERT
  N20: Part3.A2, Part10.SEL
  N21: Part3.D16/TX2, proto1.connectorA12
  N22: Part3.D17/RX2, proto1.connectorA13
  N23: Part3.D20/SDA3, proto1.connectorA8
  N24: Part3.D21/SCL3, proto1.connectorA9
  N25: Part3.IOREF, proto1.connectorW15
  N26: Part3.5V, proto1.connectorY15
  N27: Part3.GND, Part6.5A-, proto1.connectorX15
  N28: Part3.VIN, Part6.5A+
  N29: Part6.5V/AUX2, R1.Pin_0, R3.leg1, J28.pin2, LCD1.VDD
  N30: Part6.D21/SCL, proto1.connectorJ9
  N31: Part6.D20/SDA, Part6.5V/XMIN_ENDSTOP, proto1.connectorJ8, R5.Pin_0, R6.Pin_0, R7.Pin_0, R8.Pin_0, R9.Pin_0, R10.Pin_0
  N32: Part6.D19/ZMAX_ENDSTOP, Part6.D18/ZMIN_ENDSTOP, U1.Pin_4, R7.Pin_1
  N33: Part6.D15/YMAX_ENDSTOP, Part6.D14/YMIN_ENDSTOP, U3.Pin_4, R6.Pin_1
  N34: Part6.GND/AUX2, R3.leg2, J28.pin1, LCD1.VSS, LCD1.R/W, LCD1.LED+
  N35: Part6.D0, proto1.connectorJ13
  N36: Part6.D1, proto1.connectorJ12
  N37: Part6.D3/XMIN_ENDSTOP, Part6.D2/XMAX_ENDSTOP, U2.Pin_4, R5.Pin_1
  N38: Part6.D6/SERVO, J33.pin7
  N39: Part6.GND/XMIN_ENDSTOP, U1.Pin_3, U2.Pin_3, U3.Pin_3, J29.pin2, J30.pin2, J31.pin1, D2F1.COM, D2F2.COM, D2F3.NC, J33.pin10
  N40: Part6.D23/LCD_Header, J27.pin1, LCD1.RS
  N41: Part6.D25/LCD_Header, J27.pin2, LCD1.E
  N42: Part6.D27/LCD_Header, J27.pin3, LCD1.DB4
  N43: Part6.D29/LCD_Header, J27.pin4, LCD1.DB5
  N44: Part6.D31/LCD_Header, J27.pin5, LCD1.DB6
  N45: Part6.D33/LCD_Header, J27.pin6, LCD1.DB7
  N46: Part6.D35/LCD_Header, J36.pin5
  N47: Part6.D9+, J33.pin3
  N48: Part6.D9-, J33.pin9
  N49: Part6.D10+, J33.pin4
  N50: Part6.D10-, J33.pin5
  N51: Part6.GND/SERVO, J33.pin8
  N52: proto1.connectorA4, proto1.connectorC8
  N53: proto1.connectorA5, proto1.connectorD9
  N54: proto1.connectorA10, proto1.connectorW10
  N55: proto1.connectorA11, proto1.connectorX11
  N56: proto1.connectorC4, OLED1.SDA
  N57: proto1.connectorC5, OLED1.SCK
  N58: proto1.connectorD4, Part9.SDI/SDA
  N59: proto1.connectorD5, Part9.SCK/SCL
  N60: proto1.connectorE4, proto1.connectorF4
  N61: proto1.connectorE5, proto1.connectorF5
  N62: proto1.connectorJ10, proto1.connectorY10
  N63: proto1.connectorJ11, proto1.connectorZ11
  N64: proto1.connectorW1, OLED1.VDD
  N65: proto1.connectorW2, Part9.3.3V
  N66: proto1.connectorW5, Part10.VCC
  N67: proto1.connectorW6, J36.pin6
  N68: proto1.connectorX1, OLED1.GND
  N69: proto1.connectorX2, Part9.GND
  N70: proto1.connectorX5, Part10.GND
  N71: proto1.connectorX14, proto1.connectorZ14
  N72: R1.Pin_1, R4.Pin_0
  N73: R3.wiper, LCD1.V0
  N74: R4.Pin_1, LCD1.LED-
  N75: U1.Pin_1, R8.Pin_1
  N76: U1.Pin_2, J31.pin2, D2F3.COM
  N77: U2.Pin_1, R10.Pin_1
  N78: U2.Pin_2, J29.pin1, D2F1.NC, J33.pin6
  N79: U3.Pin_1, R9.Pin_1
  N80: U3.Pin_2, J30.pin1, D2F2.NC

notes:
  SCL -> Green
  SDA -> Yellow
  Motor Out
  Probe
  Air
  AIR
  D10
  Spindle
  Laser
  +
  -
  PWM
  SW1
  SW2
  Limit Switches (NC)
  To Z Spin
  A01
  A02

custom parts:
  RAMPS 1.4 Shield for Arduino Mega 2560: This ia standard Ramps 1.4 shield which is also compatible with versions 1.5 and 1.6 of the Ramps board. This model is intended only for the breadboard view, as the schematic and PCB views are not entirely accurate.
  LCD screen: A standard character display, usually with 2x16 characters. Comes in many colors.
  D2F-FL Omron Snap Action Limit Switch with Level: Snap action switch with stainless steel lever.
